// Logisim project BASIC.circ as structural Verilog: 4 circuits, main circuit Combinational
module Combinational (
  input  A,
  input  B,
  input  C
);

  wire Basic_Gates_e___a_prime_c_prime_b_prime_c, Basic_Gates_out_4, Basic_Gates_out_5, Basic_Gates_out_6,
       Basic_Gates_out_7, Basic_Gates_out_9, Basic_Gates_out_10;

  Basic_gate_Implementation Basic_Gates (
    .out_4(Basic_Gates_out_4), .out_5(Basic_Gates_out_5), .out_6(Basic_Gates_out_6),
    .out_7(Basic_Gates_out_7), .e___A_prime_C_prime_B_prime_C(Basic_Gates_e___a_prime_c_prime_b_prime_c),
    .out_9(Basic_Gates_out_9), .out_10(Basic_Gates_out_10), .A_prime(A), .B_prime(B), .C_prime(C));
  _7_Segment_Display u_7_segment_display_1 (
    .g(Basic_Gates_out_10), .f(Basic_Gates_out_9), .a(Basic_Gates_out_4), .b(Basic_Gates_out_5),
    .e(Basic_Gates_e___a_prime_c_prime_b_prime_c), .d(Basic_Gates_out_7), .c(Basic_Gates_out_6));  // open: dp
endmodule

module Basic_gate_Implementation (
  input  A_prime,
  input  B_prime,
  input  C_prime,
  output out_4,
  output out_5,
  output out_6,
  output out_7,
  output e___A_prime_C_prime_B_prime_C,
  output out_9,
  output out_10
);

  wire and_1_out, and_2_out, and_3_out, and_4_out, not_1_out, not_2_out;

  not not_1 (not_1_out, A_prime);
  not not_2 (not_2_out, B_prime);
  not not_3 (out_10, C_prime);
  and and_1 (and_1_out, not_1_out, out_10);
  and and_2 (and_2_out, not_2_out, C_prime);
  and and_3 (and_3_out, not_2_out, C_prime);
  and and_4 (and_4_out, A_prime, B_prime);
  or or_1 (out_4, not_2_out, out_10);
  or or_2 (out_6, A_prime, C_prime);
  or or_3 (out_9, and_3_out, and_4_out);
  or or_4 (out_7, not_2_out, out_10);
  or or_5 (e___A_prime_C_prime_B_prime_C, and_1_out, and_2_out);

  assign out_5 = 1'b1;

  // Notes on the sheet:
  //   A
  //   C
  //   B
  //   a= B'+C'
  //   b= 1
  //   c= C+A
  //   D= B'+C'
  //   f= B'C + AB
  //   g= C'
endmodule

module JK_FF_Seq (
  output out_1,
  output out_2,
  output out_3
);

  wire and_1_out, clock_1_out, not_1_out, not_2_out, or_1_out, or_2_out;

  Clock clock_1 (.out(clock_1_out));
  or or_1 (or_1_out, not_2_out, not_1_out);
  not not_1 (not_1_out, out_1);
  or or_2 (or_2_out, out_3, out_1);
  not not_2 (not_2_out, out_2);
  and and_1 (and_1_out, out_2, out_3);
  J_K_Flip_Flop j_k_ff_1 (.J(and_1_out), .clk(clock_1_out), .K(out_2), .Q(out_1));  // open: Qn, preset, en, reset
  J_K_Flip_Flop j_k_ff_2 (.J(out_3), .clk(clock_1_out), .K(or_2_out), .Q(out_2));  // open: Qn, preset, en, reset
  J_K_Flip_Flop j_k_ff_3 (.J(or_1_out), .clk(clock_1_out), .K(1'b1), .Q(out_3));  // open: Qn, preset, en, reset
endmodule

module Sequential (
);

  wire basic_gate_implementation_1_e___a_prime_c_prime_b_prime_c, basic_gate_implementation_1_out_4,
       basic_gate_implementation_1_out_5, basic_gate_implementation_1_out_6,
       basic_gate_implementation_1_out_7, basic_gate_implementation_1_out_9,
       basic_gate_implementation_1_out_10, jk_ff_seq_1_out_1, jk_ff_seq_1_out_2, jk_ff_seq_1_out_3;

  JK_FF_Seq jk_ff_seq_1 (.out_1(jk_ff_seq_1_out_1), .out_2(jk_ff_seq_1_out_2), .out_3(jk_ff_seq_1_out_3));
  Basic_gate_Implementation basic_gate_implementation_1 (
    .out_4(basic_gate_implementation_1_out_4), .out_5(basic_gate_implementation_1_out_5),
    .out_6(basic_gate_implementation_1_out_6), .out_7(basic_gate_implementation_1_out_7),
    .e___A_prime_C_prime_B_prime_C(basic_gate_implementation_1_e___a_prime_c_prime_b_prime_c),
    .out_9(basic_gate_implementation_1_out_9), .out_10(basic_gate_implementation_1_out_10),
    .A_prime(jk_ff_seq_1_out_1), .B_prime(jk_ff_seq_1_out_2), .C_prime(jk_ff_seq_1_out_3));
  _7_Segment_Display u_7_segment_display_1 (
    .g(basic_gate_implementation_1_out_10), .f(basic_gate_implementation_1_out_9),
    .a(basic_gate_implementation_1_out_4), .b(basic_gate_implementation_1_out_5),
    .e(basic_gate_implementation_1_e___a_prime_c_prime_b_prime_c), .d(basic_gate_implementation_1_out_7),
    .c(basic_gate_implementation_1_out_6));  // open: dp

  // Notes on the sheet:
  //   3 Bit Sequential 
  //   Circuit
  //   Basic Gate
endmodule
