// Logisim project Decoder.circ as structural Verilog: 3 circuits, main circuit Combinational 
module Combinational (
  input  [2:0] in_1
);

  wire a_out, b_out, c_out, d_out, decoder_1_out0, decoder_1_out1, decoder_1_out2, decoder_1_out3,
       decoder_1_out4, decoder_1_out5, decoder_1_out6, decoder_1_out7, e_out, f_out, g_out;

  or g (g_out, decoder_1_out6, decoder_1_out4, decoder_1_out2, decoder_1_out0);
  or f (f_out, decoder_1_out6, decoder_1_out5, decoder_1_out1);
  or e (e_out, decoder_1_out5, decoder_1_out2, decoder_1_out1, decoder_1_out0);
  _7_Segment_Display u_7_segment_display_1 (
    .g(g_out), .f(f_out), .a(a_out), .b(b_out), .e(e_out), .d(d_out), .c(c_out));  // open: dp
  or d (d_out, decoder_1_out6, decoder_1_out5, decoder_1_out4, decoder_1_out2, decoder_1_out1, decoder_1_out0);
  or c (c_out, decoder_1_out6, decoder_1_out5, decoder_1_out4, decoder_1_out3, decoder_1_out1);
  or b (b_out, decoder_1_out6, decoder_1_out5, decoder_1_out4, decoder_1_out3, decoder_1_out2, decoder_1_out1, decoder_1_out0);
  or a (a_out, decoder_1_out6, decoder_1_out5, decoder_1_out4, decoder_1_out2, decoder_1_out1, decoder_1_out0);
  Decoder #(.select(3), .enable("false")) decoder_1 (
    .out0(decoder_1_out0), .out1(decoder_1_out1), .out2(decoder_1_out2), .out3(decoder_1_out3),
    .out4(decoder_1_out4), .out5(decoder_1_out5), .out6(decoder_1_out6), .out7(decoder_1_out7), .sel(in_1));

  // Notes on the sheet:
  //   Minterm Equations: a = (1110111X)
  //   b= (11111111X)
  //   c= (0101111X )
  //   d = ( 1110111X )
  //   e = (1110010X )
  //   f= (010011X )
  //   g = (1010101X )
  //   Figure: Printed first 7 digits of ID using Decoder (Combinational)
endmodule

module Sequential (
);

  wire a_out, b_out, c_out, d_out, decoder_1_out0, decoder_1_out1, decoder_1_out2, decoder_1_out3,
       decoder_1_out4, decoder_1_out5, decoder_1_out6, decoder_1_out7, e_out, f_out, g_out;
  wire [2:0] jk_2_1_c;

  or g (g_out, decoder_1_out6, decoder_1_out4, decoder_1_out2, decoder_1_out0);
  or f (f_out, decoder_1_out6, decoder_1_out5, decoder_1_out1);
  or e (e_out, decoder_1_out5, decoder_1_out2, decoder_1_out1, decoder_1_out0);
  _7_Segment_Display u_7_segment_display_1 (
    .g(g_out), .f(f_out), .a(a_out), .b(b_out), .e(e_out), .d(d_out), .c(c_out));  // open: dp
  or d (d_out, decoder_1_out6, decoder_1_out5, decoder_1_out4, decoder_1_out2, decoder_1_out1, decoder_1_out0);
  or c (c_out, decoder_1_out6, decoder_1_out5, decoder_1_out4, decoder_1_out3, decoder_1_out1);
  or b (b_out, decoder_1_out6, decoder_1_out5, decoder_1_out4, decoder_1_out3, decoder_1_out2, decoder_1_out1, decoder_1_out0);
  or a (a_out, decoder_1_out6, decoder_1_out5, decoder_1_out4, decoder_1_out2, decoder_1_out1, decoder_1_out0);
  Decoder #(.select(3), .enable("false")) decoder_1 (
    .out0(decoder_1_out0), .out1(decoder_1_out1), .out2(decoder_1_out2), .out3(decoder_1_out3),
    .out4(decoder_1_out4), .out5(decoder_1_out5), .out6(decoder_1_out6), .out7(decoder_1_out7), .sel(jk_2_1_c));
  JK_2 jk_2_1 (.A(jk_2_1_c[2]), .B(jk_2_1_c[1]), .C(jk_2_1_c[0]));

  // Notes on the sheet:
  //   Minterm Equations: a = (1110111X)
  //   b= (11111111X)
  //   c= (0101111X )
  //   d = ( 1110111X )
  //   e = (1110010X )
  //   f= (010011X )
  //   g = (1010101X )
  //   Figure: Printed first 7 digits of ID using Decoder (Sequential)
  //   3 bit Sequential
  //   UP Counter
endmodule

module JK_2 (
  output A,
  output B,
  output C
);

  wire and_1_out, clock_1_out, not_1_out, not_2_out, or_1_out, or_2_out;

  Clock clock_1 (.out(clock_1_out));
  or or_1 (or_1_out, not_2_out, not_1_out);
  or or_2 (or_2_out, C, A);
  not not_1 (not_1_out, A);
  and and_1 (and_1_out, B, C);
  J_K_Flip_Flop j_k_ff_1 (.J(and_1_out), .clk(clock_1_out), .K(B), .Q(A));  // open: Qn, preset, en, reset
  not not_2 (not_2_out, B);
  J_K_Flip_Flop j_k_ff_2 (.J(C), .clk(clock_1_out), .K(or_2_out), .Q(B));  // open: Qn, preset, en, reset
  J_K_Flip_Flop j_k_ff_3 (.J(or_1_out), .clk(clock_1_out), .K(1'b1), .Q(C));  // open: Qn, preset, en, reset

  // Notes on the sheet:
  //   A'+B'
  //   C+A
  //   A'
  //   BC
  //   B
  //   B'
  //   C
endmodule
