// Logisim project MUX.circ as structural Verilog: 3 circuits, main circuit Combinational
module Combinational (
  input  A,
  input  B,
  input  C
);

  wire multiplexer_1_out, multiplexer_2_out, multiplexer_3_out, multiplexer_4_out, multiplexer_5_out,
       multiplexer_6_out, multiplexer_7_out, not_1_out;

  not not_1 (not_1_out, A);
  Multiplexer #(.select(2), .enable("false")) multiplexer_1 (
    .in0(1'b1), .in1(1'b1), .in2(1'b1), .in3(1'b0), .out(multiplexer_1_out), .sel({B, C}));
  Multiplexer #(.select(2), .enable("false")) multiplexer_2 (
    .in0(1'b1), .in1(1'b1), .in2(1'b1), .in3(not_1_out), .out(multiplexer_2_out), .sel({B, C}));
  Multiplexer #(.select(2), .enable("false")) multiplexer_3 (
    .in0(A), .in1(1'b1), .in2(A), .in3(not_1_out), .out(multiplexer_3_out), .sel({B, C}));
  Multiplexer #(.select(2), .enable("false")) multiplexer_4 (
    .in0(1'b1), .in1(1'b1), .in2(1'b1), .in3(1'b0), .out(multiplexer_4_out), .sel({B, C}));
  Multiplexer #(.select(2), .enable("false")) multiplexer_5 (
    .in0(not_1_out), .in1(1'b1), .in2(not_1_out), .in3(1'b0), .out(multiplexer_5_out), .sel({B, C}));
  Multiplexer #(.select(2), .enable("false")) multiplexer_6 (
    .in0(1'b0), .in1(1'b1), .in2(A), .in3(1'b0), .out(multiplexer_6_out), .sel({B, C}));
  Multiplexer #(.select(2), .enable("false")) multiplexer_7 (
    .in0(1'b1), .in1(1'b0), .in2(1'b1), .in3(1'b0), .out(multiplexer_7_out), .sel({B, C}));
  _7_Segment_Display u_7_segment_display_1 (
    .g(multiplexer_7_out), .f(multiplexer_6_out), .a(multiplexer_1_out), .b(multiplexer_2_out),
    .e(multiplexer_5_out), .d(multiplexer_4_out), .c(multiplexer_3_out));  // open: dp

  // Notes on the sheet:
  //   A'
  //   a
  //   b
  //   c
  //   d
  //   e
  //   f
  //   g
endmodule

module JK_FF_seq_Ckt (
  output out_1,
  output out_2,
  output out_3
);

  wire and_1_out, clock_1_out, not_1_out, not_2_out, or_1_out, or_2_out;

  Clock clock_1 (.out(clock_1_out));
  or or_1 (or_1_out, not_2_out, not_1_out);
  or or_2 (or_2_out, out_3, out_1);
  not not_1 (not_1_out, out_1);
  and and_1 (and_1_out, out_2, out_3);
  J_K_Flip_Flop j_k_ff_1 (.J(and_1_out), .clk(clock_1_out), .K(out_2), .Q(out_1));  // open: Qn, preset, en, reset
  not not_2 (not_2_out, out_2);
  J_K_Flip_Flop j_k_ff_2 (.J(out_3), .clk(clock_1_out), .K(or_2_out), .Q(out_2));  // open: Qn, preset, en, reset
  J_K_Flip_Flop j_k_ff_3 (.J(or_1_out), .clk(clock_1_out), .K(1'b1), .Q(out_3));  // open: Qn, preset, en, reset
endmodule

module Sequential (
);

  wire _3_bit_Sequential_Ckt_out_1, multiplexer_1_out, multiplexer_2_out, multiplexer_3_out,
       multiplexer_4_out, multiplexer_5_out, multiplexer_6_out, multiplexer_7_out, not_1_out;
  wire [1:0] _3_bit_Sequential_Ckt_out_3;

  JK_FF_seq_Ckt _3_bit_Sequential_Ckt (
    .out_1(_3_bit_Sequential_Ckt_out_1), .out_2(_3_bit_Sequential_Ckt_out_3[1]),
    .out_3(_3_bit_Sequential_Ckt_out_3[0]));
  not not_1 (not_1_out, _3_bit_Sequential_Ckt_out_1);
  Multiplexer #(.select(2), .enable("false")) multiplexer_1 (
    .in0(1'b1), .in1(1'b1), .in2(1'b1), .in3(1'b0), .out(multiplexer_1_out), .sel(_3_bit_Sequential_Ckt_out_3));
  Multiplexer #(.select(2), .enable("false")) multiplexer_2 (
    .in0(1'b1), .in1(1'b1), .in2(1'b1), .in3(not_1_out), .out(multiplexer_2_out),
    .sel(_3_bit_Sequential_Ckt_out_3));
  Multiplexer #(.select(2), .enable("false")) multiplexer_3 (
    .in0(_3_bit_Sequential_Ckt_out_1), .in1(1'b1), .in2(_3_bit_Sequential_Ckt_out_1), .in3(not_1_out),
    .out(multiplexer_3_out), .sel(_3_bit_Sequential_Ckt_out_3));
  Multiplexer #(.select(2), .enable("false")) multiplexer_4 (
    .in0(1'b1), .in1(1'b1), .in2(1'b1), .in3(1'b0), .out(multiplexer_4_out), .sel(_3_bit_Sequential_Ckt_out_3));
  Multiplexer #(.select(2), .enable("false")) multiplexer_5 (
    .in0(not_1_out), .in1(1'b1), .in2(not_1_out), .in3(1'b0), .out(multiplexer_5_out),
    .sel(_3_bit_Sequential_Ckt_out_3));
  Multiplexer #(.select(2), .enable("false")) multiplexer_6 (
    .in0(1'b0), .in1(1'b1), .in2(_3_bit_Sequential_Ckt_out_1), .in3(1'b0), .out(multiplexer_6_out),
    .sel(_3_bit_Sequential_Ckt_out_3));
  Multiplexer #(.select(2), .enable("false")) multiplexer_7 (
    .in0(1'b1), .in1(1'b0), .in2(1'b1), .in3(1'b0), .out(multiplexer_7_out), .sel(_3_bit_Sequential_Ckt_out_3));
  _7_Segment_Display u_7_segment_display_1 (
    .g(multiplexer_7_out), .f(multiplexer_6_out), .a(multiplexer_1_out), .b(multiplexer_2_out),
    .e(multiplexer_5_out), .d(multiplexer_4_out), .c(multiplexer_3_out));  // open: dp
endmodule
