// Logisim project NAND.circ as structural Verilog: 4 circuits, main circuit Combinational
module Combinational (
  input  A,
  input  B,
  input  C
);

  wire nand_1_a__b_prime_c_prime, nand_1_b__1, nand_1_e___a_prime_c_prime_b_prime_c,
       nand_1_f__b_prime_c___ab, nand_1_g__c_prime, nand_1_out_6, nand_1_out_7;

  NAND nand_1 (
    .a__B_prime_C_prime(nand_1_a__b_prime_c_prime), .b__1(nand_1_b__1), .out_6(nand_1_out_6),
    .out_7(nand_1_out_7), .e___A_prime_C_prime_B_prime_C(nand_1_e___a_prime_c_prime_b_prime_c),
    .f__B_prime_C___AB(nand_1_f__b_prime_c___ab), .g__C_prime(nand_1_g__c_prime), .A_prime(A), .B_prime(B),
    .C_prime(C));
  _7_Segment_Display u_7_segment_display_1 (
    .g(nand_1_g__c_prime), .f(nand_1_f__b_prime_c___ab), .a(nand_1_a__b_prime_c_prime), .b(nand_1_b__1),
    .e(nand_1_e___a_prime_c_prime_b_prime_c), .d(nand_1_out_7), .c(nand_1_out_6));  // open: dp

  // Notes on the sheet:
  //   UNIVERSAL GATE
  //   NAND
  //   UNIVERSAL GATE(NAND)
endmodule

module NAND (
  input  A_prime,
  input  B_prime,
  input  C_prime,
  output a__B_prime_C_prime,
  output b__1,
  output out_6,
  output out_7,
  output e___A_prime_C_prime_B_prime_C,
  output f__B_prime_C___AB,
  output g__C_prime
);

  wire nand_1_out, nand_2_out, nand_3_out, nand_4_out, nand_5_out, nand_7_out, nand_8_out, nand_10_out,
       nand_11_out, nand_13_out, nand_14_out, nand_15_out, nand_16_out, nand_17_out, nand_18_out,
       nand_19_out, nand_20_out, nand_21_out, not_1_out, not_2_out;

  not not_1 (not_1_out, A_prime);
  not not_2 (not_2_out, B_prime);
  not not_3 (g__C_prime, C_prime);
  nand nand_1 (nand_1_out, not_1_out, g__C_prime);
  nand nand_2 (nand_2_out, not_2_out, C_prime);
  nand nand_3 (nand_3_out, not_2_out, C_prime);
  nand nand_4 (nand_4_out, A_prime, B_prime);
  nand nand_5 (nand_5_out, not_2_out, not_2_out);
  nand nand_6 (a__B_prime_C_prime, nand_5_out, nand_7_out);
  nand nand_7 (nand_7_out, g__C_prime, g__C_prime);
  nand nand_8 (nand_8_out, A_prime, A_prime);
  nand nand_9 (out_6, nand_8_out, nand_10_out);
  nand nand_10 (nand_10_out, C_prime, C_prime);
  nand nand_11 (nand_11_out, not_2_out, not_2_out);
  nand nand_12 (out_7, nand_11_out, nand_13_out);
  nand nand_13 (nand_13_out, g__C_prime, g__C_prime);
  nand nand_14 (nand_14_out, nand_1_out, nand_1_out);
  nand nand_15 (nand_15_out, nand_2_out, nand_2_out);
  nand nand_16 (nand_16_out, nand_3_out, nand_3_out);
  nand nand_17 (nand_17_out, nand_4_out, nand_4_out);
  nand nand_18 (nand_18_out, nand_14_out, nand_14_out);
  nand nand_19 (nand_19_out, nand_15_out, nand_15_out);
  nand nand_20 (nand_20_out, nand_16_out, nand_16_out);
  nand nand_21 (nand_21_out, nand_17_out, nand_17_out);
  nand nand_22 (e___A_prime_C_prime_B_prime_C, nand_18_out, nand_19_out);
  nand nand_23 (f__B_prime_C___AB, nand_20_out, nand_21_out);

  assign b__1 = 1'b1;

  // Notes on the sheet:
  //   A
  //   C
  //   B
  //   A.C
  //   B.C'
  //   B.C'
  //   A'B'
  //   B
  //   C
  //   C'
  //   A'
  //   B
  //   C
  //   A'.C'
  //   B'C
  //   B'C
  //   AB
  //   c= C+A
  //   D= B'+C'
endmodule

module JK_FF_Seq (
  output out_1,
  output out_2,
  output out_3
);

  wire and_1_out, clock_1_out, not_1_out, not_2_out, or_1_out, or_2_out;

  Clock clock_1 (.out(clock_1_out));
  or or_1 (or_1_out, not_2_out, not_1_out);
  or or_2 (or_2_out, out_3, out_1);
  not not_1 (not_1_out, out_1);
  and and_1 (and_1_out, out_2, out_3);
  J_K_Flip_Flop j_k_ff_1 (.J(and_1_out), .clk(clock_1_out), .K(out_2), .Q(out_1));  // open: Qn, preset, en, reset
  not not_2 (not_2_out, out_2);
  J_K_Flip_Flop j_k_ff_2 (.J(out_3), .clk(clock_1_out), .K(or_2_out), .Q(out_2));  // open: Qn, preset, en, reset
  J_K_Flip_Flop j_k_ff_3 (.J(or_1_out), .clk(clock_1_out), .K(1'b1), .Q(out_3));  // open: Qn, preset, en, reset
endmodule

module Sequential (
);

  wire jk_ff_seq_1_out_1, jk_ff_seq_1_out_2, jk_ff_seq_1_out_3, nand_1_a__b_prime_c_prime, nand_1_b__1,
       nand_1_e___a_prime_c_prime_b_prime_c, nand_1_f__b_prime_c___ab, nand_1_g__c_prime, nand_1_out_6,
       nand_1_out_7;

  JK_FF_Seq jk_ff_seq_1 (.out_1(jk_ff_seq_1_out_1), .out_2(jk_ff_seq_1_out_2), .out_3(jk_ff_seq_1_out_3));
  NAND nand_1 (
    .a__B_prime_C_prime(nand_1_a__b_prime_c_prime), .b__1(nand_1_b__1), .out_6(nand_1_out_6),
    .out_7(nand_1_out_7), .e___A_prime_C_prime_B_prime_C(nand_1_e___a_prime_c_prime_b_prime_c),
    .f__B_prime_C___AB(nand_1_f__b_prime_c___ab), .g__C_prime(nand_1_g__c_prime),
    .A_prime(jk_ff_seq_1_out_1), .B_prime(jk_ff_seq_1_out_2), .C_prime(jk_ff_seq_1_out_3));
  _7_Segment_Display u_7_segment_display_1 (
    .g(nand_1_g__c_prime), .f(nand_1_f__b_prime_c___ab), .a(nand_1_a__b_prime_c_prime), .b(nand_1_b__1),
    .e(nand_1_e___a_prime_c_prime_b_prime_c), .d(nand_1_out_7), .c(nand_1_out_6));  // open: dp

  // Notes on the sheet:
  //   3 Bit Sequential Ckt
  //   UNIVERSAL GATE
  //   NAND
  //   Universal Gate (NAND)
endmodule
