// Logisim project Norachora.circ as structural Verilog: 2 circuits, main circuit main
module main (
  input  A,
  input  B,
  input  C
);

  wire bin_to_id_1_out_4, bin_to_id_1_out_5, bin_to_id_1_out_6, bin_to_id_1_out_7, bin_to_id_1_out_8,
       bin_to_id_1_out_9, bin_to_id_1_out_10;

  bin_to_id bin_to_id_1 (
    .out_4(bin_to_id_1_out_4), .out_5(bin_to_id_1_out_5), .out_6(bin_to_id_1_out_6),
    .out_7(bin_to_id_1_out_7), .out_8(bin_to_id_1_out_8), .out_9(bin_to_id_1_out_9),
    .out_10(bin_to_id_1_out_10), .in_1(A), .in_2(B), .in_3(C));
  _7_Segment_Display u_7_segment_display_1 (
    .g(bin_to_id_1_out_10), .f(bin_to_id_1_out_9), .a(bin_to_id_1_out_4), .b(bin_to_id_1_out_5),
    .e(bin_to_id_1_out_8), .d(bin_to_id_1_out_7), .c(bin_to_id_1_out_6));  // open: dp

  // Notes on the sheet:
  //   BASIC gate
endmodule

module bin_to_id (
  input  in_1,
  input  in_2,
  input  in_3,
  output out_4,
  output out_5,
  output out_6,
  output out_7,
  output out_8,
  output out_9,
  output out_10
);

  wire and_1_out, and_2_out, and_3_out, and_4_out, not_1_out, not_2_out;

  not not_1 (not_1_out, in_1);
  not not_2 (not_2_out, in_2);
  not not_3 (out_10, in_3);
  and and_1 (and_1_out, not_1_out, out_10);
  and and_2 (and_2_out, not_2_out, in_3);
  and and_3 (and_3_out, not_2_out, in_3);
  and and_4 (and_4_out, in_1, in_2);
  or or_1 (out_4, not_2_out, out_10);
  or or_2 (out_6, in_1, in_3);
  or or_3 (out_9, and_3_out, and_4_out);
  or or_4 (out_7, not_2_out, out_10);
  or or_5 (out_8, and_1_out, and_2_out);

  assign out_5 = 1'b1;
endmodule
