// Logisim project PROJECT-7-SEG.circ as structural Verilog: 3 circuits, main circuit main
module main (
);

  wire bin_to_id_1_a_2, bin_to_id_1_b_2, bin_to_id_1_c_2, bin_to_id_1_d, bin_to_id_1_e, bin_to_id_1_f,
       bin_to_id_1_g, jk_1_out_1, jk_1_out_2, jk_1_out_3;

  jk jk_1 (.out_1(jk_1_out_1), .out_2(jk_1_out_2), .out_3(jk_1_out_3));
  bin_to_id bin_to_id_1 (
    .A(jk_1_out_1), .B(jk_1_out_2), .C(jk_1_out_3), .a_2(bin_to_id_1_a_2), .b_2(bin_to_id_1_b_2),
    .c_2(bin_to_id_1_c_2), .d(bin_to_id_1_d), .e(bin_to_id_1_e), .f(bin_to_id_1_f), .g(bin_to_id_1_g));
  _7_Segment_Display u_7_segment_display_1 (
    .g(bin_to_id_1_g), .f(bin_to_id_1_f), .a(bin_to_id_1_a_2), .b(bin_to_id_1_b_2), .e(bin_to_id_1_e),
    .d(bin_to_id_1_d), .c(bin_to_id_1_c_2));  // open: dp
endmodule

module bin_to_id (
  input  A,
  input  B,
  input  C,
  output a_2,
  output b_2,
  output c_2,
  output d,
  output e,
  output f,
  output g
);

  wire and_1_out, and_2_out, and_3_out, and_4_out, and_5_out, not_1_out, not_2_out, not_3_out, not_4_out,
       not_5_out, not_6_out, not_7_out, not_8_out, not_9_out, not_10_out;

  not not_1 (not_1_out, B);
  not not_2 (not_2_out, C);
  or or_1 (c_2, C, A);
  not not_3 (not_3_out, B);
  not not_4 (not_4_out, C);
  not not_5 (not_5_out, A);
  not not_6 (not_6_out, B);
  not not_7 (not_7_out, A);
  not not_8 (not_8_out, C);
  not not_9 (not_9_out, B);
  not not_10 (not_10_out, B);
  not not_11 (g, C);
  or or_2 (a_2, not_1_out, not_2_out);
  or or_3 (d, not_3_out, not_4_out);
  and and_1 (and_1_out, not_5_out, not_6_out);
  and and_2 (and_2_out, not_7_out, not_8_out);
  and and_3 (and_3_out, not_9_out, C);
  and and_4 (and_4_out, not_10_out, C);
  and and_5 (and_5_out, A, B);
  or or_4 (e, and_1_out, and_2_out, and_3_out);
  or or_5 (f, and_4_out, and_5_out);

  assign b_2 = 1'b1;
endmodule

module jk (
  output out_1,
  output out_2,
  output out_3
);

  wire and_1_out, clock_1_out, not_1_out, not_2_out, or_1_out, or_2_out;

  Clock clock_1 (.out(clock_1_out));
  or or_1 (or_1_out, not_2_out, not_1_out);
  not not_1 (not_1_out, out_1);
  or or_2 (or_2_out, out_3, out_1);
  and and_1 (and_1_out, out_2, out_3);
  J_K_Flip_Flop j_k_ff_1 (.J(and_1_out), .clk(clock_1_out), .K(out_2), .Q(out_1));  // open: Qn, preset, en, reset
  not not_2 (not_2_out, out_2);
  J_K_Flip_Flop j_k_ff_2 (.J(out_3), .clk(clock_1_out), .K(or_2_out), .Q(out_2));  // open: Qn, preset, en, reset
  J_K_Flip_Flop j_k_ff_3 (.J(or_1_out), .clk(clock_1_out), .K(1'b1), .Q(out_3));  // open: Qn, preset, en, reset
endmodule
