// Logisim project Self basic.circ as structural Verilog: 3 circuits, main circuit main
module main (
  input  in_1,
  input  in_2,
  input  in_3
);

  wire new_1_p4, new_1_p5, new_1_p6, new_1_p7, new_1_p8, new_1_p9, new_1_p10;

  // NEW new_1: pin names not known; wires that end beside it: in_1, in_2, in_3, new_1_p4, new_1_p5, new_1_p6, new_1_p7, new_1_p8, new_1_p9, new_1_p10
  _7_Segment_Display u_7_segment_display_1 (
    .g(new_1_p10), .f(new_1_p9), .a(new_1_p4), .b(new_1_p5), .e(new_1_p8), .d(new_1_p7), .c(new_1_p6));  // open: dp
endmodule

module Circuit (
  input  A,
  input  B,
  input  C,
  output a_2,
  output b_2,
  output c_2,
  output d,
  output e,
  output f,
  output g
);

  wire and_1_out, and_2_out, and_3_out, and_4_out, not_1_out, not_2_out;

  not not_1 (not_1_out, B);
  not not_2 (not_2_out, A);
  not not_3 (g, C);
  and and_1 (and_1_out, not_2_out, g);
  and and_2 (and_2_out, not_1_out, C);
  and and_3 (and_3_out, not_1_out, C);
  and and_4 (and_4_out, A, B);
  or or_1 (a_2, not_1_out, g);
  or or_2 (c_2, C, A);
  or or_3 (d, not_1_out, g);
  or or_4 (e, and_1_out, and_2_out);
  or or_5 (f, and_3_out, and_4_out);

  assign b_2 = 1'b1;
endmodule

module NEW (
  input  A,
  input  B,
  input  C,
  output a_2,
  output b_2,
  output c_2,
  output d,
  output e,
  output f,
  output g
);

  wire and_1_out, and_2_out, and_3_out, and_4_out, not_1_out, not_2_out;

  not not_1 (not_1_out, B);
  not not_2 (not_2_out, A);
  not not_3 (g, C);
  and and_1 (and_1_out, not_2_out, g);
  and and_2 (and_2_out, not_1_out, C);
  and and_3 (and_3_out, not_1_out, C);
  and and_4 (and_4_out, A, B);
  or or_1 (a_2, not_1_out, g);
  or or_2 (c_2, C, A);
  or or_3 (d, not_1_out, g);
  or or_4 (e, and_1_out, and_2_out);
  or or_5 (f, and_3_out, and_4_out);

  assign b_2 = 1'b1;
endmodule
