// Logisim project dsadaa.circ as structural Verilog
module _3_bi_7_seg (
  input  A,
  input  B,
  input  C,
  output a_2,
  output b_2,
  output c_2,
  output d,
  output e,
  output f,
  output g
);

  wire and_1_out, and_2_out, and_3_out, and_4_out, and_5_out, and_6_out, not_1_out, not_2_out, not_3_out,
       not_4_out, not_5_out, not_6_out, not_7_out, not_8_out, not_9_out, not_10_out, not_11_out;

  not not_1 (not_1_out, B);
  not not_2 (not_2_out, C);
  or or_1 (c_2, C, A);
  not not_3 (not_3_out, B);
  not not_4 (not_4_out, C);
  not not_5 (not_5_out, A);
  not not_6 (not_6_out, C);
  not not_7 (not_7_out, B);
  not not_8 (not_8_out, B);
  not not_9 (not_9_out, A);
  not not_10 (not_10_out, C);
  not not_11 (not_11_out, C);
  or or_2 (a_2, not_1_out, not_2_out);
  or or_3 (d, not_3_out, not_4_out);
  and and_1 (and_1_out, not_5_out, not_6_out);
  and and_2 (and_2_out, not_7_out, C);
  and and_3 (and_3_out, not_8_out, C);
  and and_4 (and_4_out, A, B);
  and and_5 (and_5_out, not_9_out, not_10_out);
  and and_6 (and_6_out, B, not_11_out);
  or or_4 (d, and_1_out, and_2_out);
  or or_5 (f, and_3_out, and_4_out);
  or or_6 (f, and_5_out, and_6_out);
  _7_Segment_Display u_7_segment_display_1 (.g(f), .f(f), .a(a_2), .b(1'b1), .e(d), .d(d), .c(c_2));  // open: dp

  assign b_2 = 1'b1;
  assign e = d;
  assign g = f;
endmodule

module \new  (
  input  A,
  input  B,
  input  C,
  output a_2,
  output b_2,
  output c_2,
  output d,
  output e,
  output f,
  output g
);

  wire and_1_out, and_2_out, and_3_out, and_4_out, not_1_out, not_2_out, not_3_out, not_4_out, not_5_out,
       not_6_out, not_7_out, not_8_out;

  not not_1 (not_1_out, B);
  not not_2 (not_2_out, C);
  or or_1 (c_2, C, A);
  not not_3 (not_3_out, B);
  not not_4 (not_4_out, C);
  not not_5 (not_5_out, A);
  not not_6 (not_6_out, C);
  not not_7 (not_7_out, B);
  not not_8 (not_8_out, B);
  not not_9 (g, C);
  or or_2 (a_2, not_1_out, not_2_out, A);
  or or_3 (d, not_3_out, not_4_out);
  and and_1 (and_1_out, not_5_out, not_6_out);
  and and_2 (and_2_out, not_7_out, C);
  and and_3 (and_3_out, not_8_out, C);
  and and_4 (and_4_out, A, B);
  or or_4 (e, and_1_out, and_2_out);
  or or_5 (f, and_3_out, and_4_out);

  assign b_2 = 1'b1;
endmodule
